# Fritzing sketch 1-Wire Arduino Master Slave (saved by Fritzing 0.8.7b)

parts:
  Part1 = Arduino Nano (Rev3.0)
  R3 = Resistor [tolerance=±5% resistance=4.7k package=THT]
  Part2 = Arduino Nano (Rev3.0)

nets:
  GND: Part1.GND, Part2.GND
  N1: Part1.D10, R3.Pin_0, Part2.D2
  N2: Part1.5V, R3.Pin_1

notes:
  master
  slave
  4k7
  5v
  GND
  1-Wire bus
